# Fritzing sketch Oxygen_Saturation (saved by Fritzing 1.0.6)
breadboards: 1

parts:
  U1 = ESP32S-HiLetgo [part_number=ESP32S-HiLetgo]
  M1 = MakerFocus MAX30102
  OLED_I2C1 = OLED 128x64 I2C Monochrome Display
  J1 = Piezo Speaker  # not connected

nets:
  GND: U1.GND, M1.GND, OLED_I2C1.GND
  N1: U1.GPIO21, M1.IRQ, OLED_I2C1.SDA
  N2: U1.GPIO22, M1.RD, OLED_I2C1.SCK
  N3: M1.INT, OLED_I2C1.VDD

custom parts:
  ESP32S-HiLetgo: HiLetgo ESP-WROOM-32 ESP32 ESP-32S Development Board 2.4GHz Dual-Mode WiFi + Bluetooth Dual Cores Microcontroller The ESP32 integrated with Antenna switches, RF Balun, power amplifiers, low-noise amplifiers, filters, and management modules, and the entire solution occupies the least area of PCB. 2.4 GHz Wi-Fi plus Bluetooth dual-mode chip, with TSMC Ultra-low power consumption 40nm technology,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
  MakerFocus MAX30102: Oximeter module using the MAX30102 chip. As usual, if you want the mounting holes in pcb, you need to drag a hole over the pad in silkscreen to actually drill the hole (by default they are not drilled)
